# Fritzing sketch pump-driver-schematic-1 (saved by Fritzing 0.9.3b)
breadboards: 1

parts:
  Q1 = Basic FET N-Channel [package="TO220 [THT]"]
  Q2 = NPN-Transistor [package="TO92 [THT]"]
  R1 = Resistor [tolerance=±5% resistance=10k package=THT]
  D1 = Rectifier Diode [part_number=1N4001 package="300 mil [THT]"]
  M1 = DC Motor
  R2 = Resistor [tolerance=±5% resistance=100 package=THT]
  12V_power_plug = Power plug

nets:
  N1: Q1.gate, Q2.C, R1.Pin_1
  N2: Q1.drain, D1.cathode, M1.pin_1
  12V: Q1.source, R1.Pin_0, 12V_power_plug.VCC
  GND: Q2.E, D1.anode, M1.pin_2, 12V_power_plug.GND
  N3: Q2.B, R2.Pin_1
  motor control input: R2.Pin_0
